// Logisim project circuit-02-01.circ as structural Verilog: 1 circuit, main circuit main
module main (
  input  x0,
  input  x1,
  input  f,
  input  a,
  input  g,
  input  b,
  input  x2,
  input  x3,
  input  in_9,
  input  d,
  input  c
);

  wire and_1_out, and_2_out, and_3_out, and_4_out, and_5_out, and_6_out, and_7_out, and_8_out, and_9_out,
       and_10_out, and_11_out, and_12_out, not_1_out, not_2_out, not_3_out, not_4_out, not_5_out, not_6_out,
       not_7_out, not_8_out, not_9_out, not_10_out, not_11_out, not_12_out, or_1_out, or_2_out, or_3_out;

  not not_1 (not_1_out, x0);
  and and_1 (and_1_out, not_1_out, not_2_out);
  not not_2 (not_2_out, x1);
  not not_3 (not_3_out, x2);
  and and_2 (and_2_out, not_3_out, not_4_out);
  not not_4 (not_4_out, x3);
  not not_5 (not_5_out, x0);
  and and_3 (and_3_out, not_5_out, x1);
  not not_6 (not_6_out, x2);
  and and_4 (and_4_out, not_6_out, not_7_out);
  not not_7 (not_7_out, x3);
  not not_8 (not_8_out, x0);
  and and_5 (and_5_out, not_8_out, x1);
  and and_6 (and_6_out, x2, not_9_out);
  not not_9 (not_9_out, x3);
  not not_10 (not_10_out, x0);
  and and_7 (and_7_out, not_10_out, not_11_out);
  not not_11 (not_11_out, x1);
  not not_12 (not_12_out, x2);
  and and_8 (and_8_out, not_12_out, x3);
  and and_9 (and_9_out, and_1_out, and_2_out);
  and and_10 (and_10_out, and_3_out, and_4_out);
  and and_11 (and_11_out, and_5_out, and_6_out);
  and and_12 (and_12_out, and_7_out, and_8_out);
  or or_1 (or_1_out, and_9_out, and_10_out);
  or or_2 (or_2_out, and_11_out, and_12_out);
  or or_3 (or_3_out, or_1_out, or_2_out);
  _7_Segment_Display u_7_segment_display_1 (.g(g), .f(f), .a(a), .b(b), .e(or_3_out), .d(d), .c(c), .dp(in_9));
endmodule
