// Logisim project circuit-04-01.circ as structural Verilog: 1 circuit, main circuit main
module main (
  input  s0,
  input  x0,
  input  x1,
  output d0
);

  wire and_1_out, and_2_out, not_1_out;

  not not_1 (not_1_out, s0);
  and and_1 (and_1_out, not_1_out, x0);
  and and_2 (and_2_out, s0, x1);
  or or_1 (d0, and_1_out, and_2_out);
endmodule
