// Logisim project 2.circ as structural Verilog: 1 circuit, main circuit main
module main (
  input  A,
  input  B,
  output out_3,
  output out_4,
  output out_5
);

  nand nand_1 (out_3, A, A);
  nand nand_2 (out_5, B, B);
  nand nand_3 (out_4, out_3, out_5);
endmodule
