// Logisim project circuit-01-01.circ as structural Verilog: 1 circuit, main circuit main
module main (
  input  i0,
  input  s0,
  input  i1,
  output out_4
);

  wire and_1_out, and_2_out, not_1_out;

  not not_1 (not_1_out, s0);
  and and_1 (and_1_out, i0, i0, not_1_out);
  and and_2 (and_2_out, s0, i1, i1);
  or or_1 (out_4, and_1_out, and_2_out);
endmodule
